// Logisim project 4008.circ as structural Verilog: 7 circuits, main circuit main
module main (
  input  [3:0] Zahl_1,
  input  [3:0] Operation,
  input  [3:0] Zahl_2,
  output [15:0] \Ergäbnis 
);

  wire clock_1_out;

  Clock clock_1 (.out(clock_1_out));
  cpu cpu_1 (.in_1(Zahl_1), .in_2(Operation), .in_3(Zahl_2), .out_5(\Ergäbnis ), .in_4(clock_1_out));

  // Notes on the sheet:
  //   Operationen:
  //   001 - Plus
  //   010 - Minus
  //   100 - Geteilt
  //   011 - Mal
endmodule

module register_befehle (
  input  [3:0] Befehlsbus,
  input  [3:0] in_2,
  input  [3:0] in_3,
  input  in_4,
  output [3:0] Zahl_1,
  output [3:0] Zahl_2,
  output out_7,
  output out_8,
  output out_9,
  output out_10
);

  Comparator #(.width(4)) comparator_1 (.a(in_2), .b(4'b0001), .eq(out_7));  // open: gt, lt
  Comparator #(.width(4)) comparator_2 (.a(in_2), .b(4'b0010), .eq(out_8));  // open: gt, lt
  Comparator #(.width(4)) comparator_3 (.a(in_2), .b(4'b0011), .eq(out_9));  // open: gt, lt
  Comparator #(.width(4)) comparator_4 (.a(in_2), .b(4'b0100), .eq(out_10));  // open: gt, lt
  Register #(.width(4)) register_1 (.D(Befehlsbus), .Q(Zahl_1), .clk(in_4));  // open: en, clr
  Register #(.width(4)) register_2 (.D(in_3), .Q(Zahl_2), .clk(in_4));  // open: en, clr

  // Notes on the sheet:
  //   -
  //   ROM
  //   +
  //   *
  //   /
  //   A
  //   B
endmodule

module plus (
  input  [3:0] in_1,
  input  [3:0] in_2,
  input  in_3,
  input  in_4,
  output [3:0] out_5
);

  wire [3:0] adder_1_out, register_1_q;

  Register #(.width(4)) register_1 (.D(adder_1_out), .Q(register_1_q), .clk(in_3));  // open: en, clr
  assign out_5 = in_4 ? register_1_q : 4'bz;  // Controlled_Buffer controlled_buffer_1
  Adder #(.width(4)) adder_1 (.a(in_1), .b(in_2), .out(adder_1_out));  // open: cin, cout
endmodule

module minus (
  input  [3:0] in_1,
  input  [3:0] in_2,
  input  in_3,
  input  in_4,
  output [3:0] out_5
);

  wire [3:0] register_1_q, subtractor_1_out;

  Subtractor #(.width(4)) subtractor_1 (.a(in_1), .b(in_2), .out(subtractor_1_out));  // open: bin, bout
  assign out_5 = in_4 ? register_1_q : 4'bz;  // Controlled_Buffer controlled_buffer_1
  Register #(.width(4)) register_1 (.D(subtractor_1_out), .Q(register_1_q), .clk(in_3));  // open: en, clr
endmodule

module cpu (
  input  [3:0] in_1,
  input  [3:0] in_2,
  input  [3:0] in_3,
  input  in_4,
  output [15:0] out_5
);

  wire register_befehle_1_out_7, register_befehle_1_out_8, register_befehle_1_out_9,
       register_befehle_1_out_10;
  wire [3:0] register_befehle_1_zahl_1, register_befehle_1_zahl_2;

  register_befehle register_befehle_1 (
    .Befehlsbus(in_1), .in_2(in_2), .in_3(in_3), .in_4(in_4), .Zahl_1(register_befehle_1_zahl_1),
    .Zahl_2(register_befehle_1_zahl_2), .out_7(register_befehle_1_out_7), .out_8(register_befehle_1_out_8),
    .out_9(register_befehle_1_out_9), .out_10(register_befehle_1_out_10));
  plus plus_1 (
    .in_1(register_befehle_1_zahl_1), .in_2(register_befehle_1_zahl_2), .in_3(in_4),
    .in_4(register_befehle_1_out_7), .out_5(out_5[3:0]));
  minus minus_1 (
    .in_1(register_befehle_1_zahl_1), .in_2(register_befehle_1_zahl_2), .in_3(in_4),
    .in_4(register_befehle_1_out_8), .out_5(out_5[7:4]));
  mal mal_1 (
    .in_1(register_befehle_1_zahl_1), .in_2(register_befehle_1_zahl_2), .in_3(in_4),
    .in_4(register_befehle_1_out_9), .out_5(out_5[11:8]));
  dividieren dividieren_1 (
    .in_1(register_befehle_1_zahl_1), .in_2(register_befehle_1_zahl_2), .in_3(in_4),
    .in_4(register_befehle_1_out_10), .out_5(out_5[15:12]));
endmodule

module mal (
  input  [3:0] in_1,
  input  [3:0] in_2,
  input  in_3,
  input  in_4,
  output [3:0] out_5
);

  wire [3:0] multiplier_1_out, register_1_q;

  assign out_5 = in_4 ? register_1_q : 4'bz;  // Controlled_Buffer controlled_buffer_1
  Register #(.width(4)) register_1 (.D(multiplier_1_out), .Q(register_1_q), .clk(in_3));  // open: en, clr
  Multiplier #(.width(4)) multiplier_1 (.a(in_1), .b(in_2), .out(multiplier_1_out));  // open: cin, cout
endmodule

module dividieren (
  input  [3:0] in_1,
  input  [3:0] in_2,
  input  in_3,
  input  in_4,
  output [3:0] out_5
);

  wire [3:0] divider_1_out, register_1_q;

  Register #(.width(4)) register_1 (.D(divider_1_out), .Q(register_1_q), .clk(in_3));  // open: en, clr
  Divider #(.width(4)) divider_1 (.a(in_1), .b(in_2), .out(divider_1_out));  // open: upper, rem
  assign out_5 = in_4 ? register_1_q : 4'bz;  // Controlled_Buffer controlled_buffer_1
endmodule
